# Fritzing sketch 8ball (saved by Fritzing 0.9.3b)
breadboards: 1

parts:
  Part1 = Adafruit Feather HUZZAH ESP8266 [part_number="Adafruit #2821"]
  Part2 = Adafruit 1.44 inch TFT Breakout [part_number="Adafruit #2088"]
  Part3 = Adafruit LIS3DH [part_number="Adafruit #2809"]

nets:
  N1: Part1.GPIO12/MISO, Part3.SDO
  N2: Part1.GPIO13/MOSI, Part2.MOSI, Part3.SDA
  N3: Part1.GPIO14/SCK, Part2.SCK, Part3.SCL
  GND: Part1.GND, Part2.GND, Part3.GND
  VIN: Part1.3.3V, Part2.VIN, Part3.VIN
  N4: Part1.RESET, Part2.RESET
  N5: Part1.GPIO15, Part3.CS
  N6: Part1.GPIO0, Part2.LITE
  N7: Part1.GPIO16, Part2.TFTCS
  N8: Part1.GPIO2, Part2.TFTDC

custom parts:
  Adafruit Feather HUZZAH ESP8266: his is the Adafruit Feather HUZZAH ESP8266 - our take on an 'all-in-one' ESP8266 WiFi development board with built in USB and battery charging. Its an ESP8266 WiFi module with all the extras you need, ready to rock! We have other boards in the Feather family, check'em out here. At the Feather HUZZAH's heart is an ESP8266 WiFi microcontroller clocked at 80 MHz and at 3.3V logic. This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
  Adafruit 1.44 inch TFT Breakout: This lovely little display breakout is the best way to add a small, colorful and bright display to any project. Since the display uses 4-wire SPI to communicate and has its own pixel-addressable frame buffer, it can be used with every kind of microcontroller. Even a very small one with low memory and few pins available! The 1.44" display has 128x128 color pixels. Unlike the low cost "Nokia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
  Adafruit LIS3DH: The LIS3DH is a very popular low power triple-axis accelerometer. It's low-cost, but has just about every 'extra' you'd want in an accelerometer: Three axis sensing, 10-bit precision ±2g/±4g/±8g/±16g selectable scaling Both I2C (2 possible addresses) and SPI interface options Interrupt output Multiple data rate options 1 Hz to 5Khz As low as 2uA current draw (just the chip itself, not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
